# Fritzing sketch Connection_diagram (saved by Fritzing 0.9.3b)
breadboards: 1

parts:
  M1 = DC Motor
  S2 = H-Bridge with L298N
  M2 = DC Motor
  HC-SR04_Sensor_1 = HC-SR04 Ultrasonic Distance Sensor
  Part2 = Arduino Uno (Rev3) - ICSP
  U1 = ESP32-38PinWide [part_number=ESP32-38PinWide]
  M5 = fc-51 [package=THT]
  M6 = fc-51 [package=THT]
  M7 = fc-51 [package=THT]
  S3 = Toggle Switch [package=THT]
  BATT1 = LiPoly Battery (1300mAh)  # not connected
  VCC1 = 4 x AA Battery Box
  M4 = Dagu DGServo 9g (Top view) [part_number=RS001B]

nets:
  N1: M1.pin_2, S2.M2-01
  N2: S2.12V, S3.COM
  N3: S2.GND, VCC1.-
  5V: S2.5V, HC-SR04_Sensor_1.VCC, Part2.5V, M5.pin3, M6.pin3, M7.pin3, M4.vcc
  N4: S2.ENA, Part2.A3
  N5: S2.IN1, Part2.D12/MISO
  N6: S2.IN2, Part2.D11_PWM/MOSI
  N7: S2.IN3, Part2.D10_PWM/SS
  N8: S2.IN4, Part2.D9_PWM
  N9: S2.ENB, Part2.A2
  N10: S2.M1-01, M2.pin_2
  N11: S2.M1-02, M2.pin_1
  N12: HC-SR04_Sensor_1.TRIG, Part2.D5_PWM
  N13: HC-SR04_Sensor_1.ECHO, Part2.D4
  GND: HC-SR04_Sensor_1.GND, Part2.GND, U1.GND, M5.pin2, M6.pin2, M7.pin2, M4.gnd
  N14: Part2.A4/SDA, U1.GPIO21
  N15: Part2.A5/SCL, U1.GPIO22
  N16: Part2.D2, M6.pin1
  N17: Part2.D3_PWM, M7.pin1
  N18: Part2.D6_PWM, M4.pulse
  N19: Part2.3V3, U1.3.3
  N20: U1.GPIO2, M5.pin1
  N21: S3.L1, VCC1.+

custom parts:
  H-Bridge with L298N: h-bridge
  ESP32-38PinWide: Generic 38-Pin ESP32 with wide format (only access to one side of pins on a breadboard) based on Stephen Lilley's HiLetgo ESP-WROOM-32 ESP32 ESP-32S Development Board.
  LiPoly Battery (1300mAh): Lithium Ion Polymer Battery (1300mAh)
  4 x AA Battery Box: A 4 x AA battery box.
